// Logisim project pdp8processor.circ as structural Verilog: 9 circuits, main circuit main
module main (
  output [6:0] MAIN_TTY_OUT,
  output [7:0] MAIN_PC_OUT
);

  wire alu_basic_inst_1_link_out, alu_grp1_1_link_out, and_1_out, and_2_out, and_3_out, and_4_out, and_5_out,
       and_6_out, BIT0, BIT1, BIT2, CLK, comparator_1_eq, DR, ex_out_logic_1_lnk_sel, GROUP, IR, LINK_OUT,
       LINK_q, MEM_ACC, MEM_WB, multiplexer_3_out, not_1_out, or_1_out, or_2_out, PC_t, WB, wb_1_acc_wb,
       wb_1_link_wb;
  wire [1:0] ex_out_logic_1_acc_sel2, ex_out_logic_1_pc_sel2, mem_sel_logic_1_mem_sel2;
  wire [2:0] OPCODE;
  wire [7:0] adder_1_out, alu_basic_inst_1_next_pc, alu_grp2_1_pcout, GRPMINST, INFERENCE, M_a,
       multiplexer_1_out, multiplexer_2_out, multiplexer_5_out, PC_OUT;
  wire [11:0] ACC_OUT, ACC_q, alu_basic_inst_1_acc_out, alu_basic_inst_1_data_out, alu_grp1_1_acc_out,
       alu_grp2_1_accout, DATA110, DATA_OUT, multiplexer_4_out, ram_1_data;

  Clock u_CLK (.out(CLK));
  Register #(.trigger("falling")) PC (.D(PC_OUT), .en(PC_t), .Q(MAIN_PC_OUT), .clk(CLK));  // open: clr
  CU cu_1 (
    .OPCODE_11(OPCODE[2]), .OPCODE_10(OPCODE[1]), .OPCODE_9(OPCODE[0]), .CLOCK(CLK), .PC(PC_t), .IR(IR),
    .DR(DR), .WB(WB), .S1(BIT2), .S2(BIT1), .S3(BIT0), .MEM_ACC(MEM_ACC));
  and and_1 (and_1_out, ~BIT0, BIT1, ~BIT2, GROUP);  // AND_Gate
  MEM_SEL_LOGIC mem_sel_logic_1 (
    .IB(GROUP), .STATE2(and_1_out), .STATE4(and_2_out), .MEM_SEL(mem_sel_logic_1_mem_sel2[1]),
    .MEM_SEL2(mem_sel_logic_1_mem_sel2[0]));
  and and_2 (and_2_out, ~BIT0, ~BIT1, BIT2, GROUP);  // AND_Gate
  // Probe on MAIN_PC_OUT
  or or_1 (or_1_out, MEM_ACC, MEM_WB);
  Multiplexer #(.select(2), .width(8), .enable("false")) multiplexer_1 (
    .in0(GRPMINST), .in1(INFERENCE), .in2(M_a), .out(multiplexer_1_out), .sel(mem_sel_logic_1_mem_sel2));  // open: in3
  // Probe on multiplexer_1_out
  Bit_Extender #(.in_width(12), .out_width(7)) bit_extender_1 (.in(DATA_OUT), .out(MAIN_TTY_OUT));
  and and_3 (and_3_out, ~OPCODE[0], OPCODE[1], OPCODE[2], BIT2, ~BIT1, ~BIT0);  // AND_Gate
  // Probe on multiplexer_2_out
  Multiplexer #(.width(8), .enable("false")) multiplexer_2 (
    .in0(MAIN_PC_OUT), .in1(multiplexer_1_out), .out(multiplexer_2_out), .sel(or_1_out));
  TTY tty_1 (.data(MAIN_TTY_OUT), .clk(CLK), .we(and_3_out), .clr(and_4_out));
  Comparator #(.width(7)) comparator_1 (.a(MAIN_TTY_OUT), .b(7'b0011011), .eq(comparator_1_eq));  // open: gt, lt
  and and_4 (and_4_out, comparator_1_eq, and_3_out);
  // Probe on DATA_OUT
  // Probe on {BIT2, BIT1, BIT0}
  not not_1 (not_1_out, MEM_WB);
  // Probe on ram_1_data
  RAM #(.dataWidth(12), .bus("separate")) ram_1 (
    .addr(multiplexer_2_out), .din(DATA_OUT), .data(ram_1_data), .str(MEM_WB), .clk(CLK), .ld(not_1_out));  // open: sel, clr
  Register #(.width(12)) INST (.D(ram_1_data), .en(IR), .Q({OPCODE, GROUP, GRPMINST}), .clk(CLK));  // open: clr
  and and_5 (and_5_out, ~BIT0, BIT1, ~BIT2, GROUP, DR);  // AND_Gate
  and and_6 (and_6_out, BIT0, ~BIT1, ~BIT2, DR);  // AND_Gate
  or or_2 (or_2_out, and_5_out, and_6_out);
  Register #(.width(12)) DATA (.D(ram_1_data), .en(or_2_out), .Q(DATA110), .clk(CLK));  // open: clr
  Register register_1 (.D(INFERENCE), .en(and_5_out), .Q(M_a), .clk(CLK));  // open: clr
  // Probe on {BIT2, BIT1, BIT0}
  Bit_Extender #(.in_width(12), .out_width(8)) bit_extender_2 (.in(DATA110), .out(INFERENCE));
  WB wb_1 (
    .WB(WB), .GRP_IB(GROUP), .OPCODE1(OPCODE[2]), .OPCODE2(OPCODE[1]), .OPCODE3(OPCODE[0]),
    .LINK_WB(wb_1_link_wb), .ACC_WB(wb_1_acc_wb), .MEM_WB(MEM_WB));
  Register #(.width(1)) LINK (.D(LINK_OUT), .en(wb_1_link_wb), .Q(LINK_q), .clk(CLK));  // open: clr
  Register #(.width(12)) ACC (.D(ACC_OUT), .en(wb_1_acc_wb), .Q(ACC_q), .clk(CLK));  // open: clr
  EX_OUT_LOGIC ex_out_logic_1 (
    .GRP(GROUP), .LNK_SEL(ex_out_logic_1_lnk_sel), .OPCODE1(OPCODE[2]), .ACC_SEL(ex_out_logic_1_acc_sel2[1]),
    .OPCODE2(OPCODE[1]), .OPCODE3(OPCODE[0]), .ACC_SEL2(ex_out_logic_1_acc_sel2[0]),
    .PC_SEL(ex_out_logic_1_pc_sel2[1]), .PC_SEL2(ex_out_logic_1_pc_sel2[0]));
  ALU_BASIC_INST alu_basic_inst_1 (
    .LINK(LINK_q), .ACC(ACC_q), .DATA(DATA110), .PC(MAIN_PC_OUT), .MEM_ADDR(GRPMINST), .ALU_CONTROL(OPCODE),
    .LINK_OUT(alu_basic_inst_1_link_out), .ACC_OUT(alu_basic_inst_1_acc_out),
    .DATA_OUT(alu_basic_inst_1_data_out), .NEXT_PC(alu_basic_inst_1_next_pc), .IB(GROUP), .M_a(M_a));
  ALU_GRP1 alu_grp1_1 (
    .MINTS(GRPMINST), .LINK(LINK_q), .ACC(ACC_q), .ACC_OUT(alu_grp1_1_acc_out), .LINK_OUT(alu_grp1_1_link_out));
  ALU_GRP2 alu_grp2_1 (
    .ACCout(alu_grp2_1_accout), .Instruction(GRPMINST), .ACC(ACC_q), .LNK(LINK_q), .PC(MAIN_PC_OUT),
    .PCout(alu_grp2_1_pcout));
  // Probe on ex_out_logic_1_pc_sel2
  Adder adder_1 (.a(MAIN_PC_OUT), .b(8'h1), .out(adder_1_out));  // open: cin, cout
  // AND_Gate and_7 has open pins: in0=BIT2, in1=BIT1, in2=BIT0, out=open
  Multiplexer #(.enable("false")) multiplexer_3 (
    .in0(alu_basic_inst_1_link_out), .in1(alu_grp1_1_link_out), .out(multiplexer_3_out),
    .sel(ex_out_logic_1_lnk_sel));
  Multiplexer #(.select(2), .width(12), .enable("false")) multiplexer_4 (
    .in0(alu_basic_inst_1_acc_out), .in1(alu_grp1_1_acc_out), .in2(alu_grp2_1_accout),
    .out(multiplexer_4_out), .sel(ex_out_logic_1_acc_sel2));  // open: in3
  // Probe on alu_basic_inst_1_data_out
  Multiplexer #(.select(2), .width(8), .enable("false")) multiplexer_5 (
    .in0(adder_1_out), .in1(alu_basic_inst_1_next_pc), .in2(alu_grp2_1_pcout), .out(multiplexer_5_out),
    .sel(ex_out_logic_1_pc_sel2));  // open: in3
  Register #(.width(1), .trigger("falling")) u_LINK_OUT (
    .D(multiplexer_3_out), .Q(LINK_OUT), .clk(CLK));  // open: en, clr
  Register #(.width(12), .trigger("falling")) u_ACC_OUT (
    .D(multiplexer_4_out), .Q(ACC_OUT), .clk(CLK));  // open: en, clr
  Register #(.width(12), .trigger("falling")) u_DATA_OUT (
    .D(alu_basic_inst_1_data_out), .Q(DATA_OUT), .clk(CLK));  // open: en, clr
  Register #(.trigger("falling")) u_PC_OUT (.D(multiplexer_5_out), .Q(PC_OUT), .clk(CLK));  // open: en, clr
  // Probe on ex_out_logic_1_acc_sel2

  // Other names for the same wires on the sheet: MEMADDR[7:0] = GRPMINST; IB = GROUP; PC[7:0] = MAIN_PC_OUT;
  //   TTY[6:0] = MAIN_TTY_OUT
endmodule

module CU (
  input  CLOCK,
  input  OPCODE_11,
  input  OPCODE_10,
  input  OPCODE_9,
  output PC,
  output MEM_ACC,
  output IR,
  output DR,
  output WB,
  output S1,
  output S2,
  output S3
);

  wire S1_NEXT, S2_NEXT, S3_NEXT;

  D_Flip_Flop d_ff_1 (.clk(CLOCK), .D(S1_NEXT), .Q(S1), .preset(1'b0), .en(1'b1), .reset(1'b0));  // open: Qn
  D_Flip_Flop d_ff_2 (.clk(CLOCK), .D(S2_NEXT), .Q(S2), .preset(1'b0), .en(1'b1), .reset(1'b0));  // open: Qn
  D_Flip_Flop d_ff_3 (.clk(CLOCK), .D(S3_NEXT), .Q(S3), .preset(1'b0), .en(1'b1), .reset(1'b0));  // open: Qn
  CU_Logic cu_logic_1 (
    .OPCODE1(OPCODE_11), .S1_NEXT(S1_NEXT), .OPCODE2(OPCODE_10), .OPCODE3(OPCODE_9), .S1(S1), .S2(S2),
    .S2_NEXT(S2_NEXT), .S3(S3), .S3_NEXT(S3_NEXT), .PC(PC), .MEM_ACC(MEM_ACC), .IR(IR), .DR(DR), .WB(WB));

  // Other names for the same wires on the sheet: CLK = CLOCK
endmodule

module CU_Logic (
  input  OPCODE1,
  input  OPCODE2,
  input  OPCODE3,
  input  S1,
  input  S2,
  input  S3,
  output S1_NEXT,
  output S2_NEXT,
  output S3_NEXT,
  output PC,
  output MEM_ACC,
  output IR,
  output DR,
  output WB
);

  wire and_1_out, and_2_out, and_3_out, and_4_out, and_5_out, and_6_out, and_7_out, and_8_out, and_11_out,
       and_12_out, not_1_out, not_2_out, not_3_out, not_4_out, not_5_out, not_6_out, not_7_out, not_8_out,
       not_9_out, not_10_out, not_11_out, not_12_out, not_13_out, not_14_out, not_15_out, not_16_out,
       not_17_out, not_18_out, not_19_out;

  and and_1 (and_1_out, S2, S3);
  and and_2 (and_2_out, OPCODE1, OPCODE2, OPCODE3, S3);
  not not_1 (not_1_out, OPCODE1);
  not not_2 (not_2_out, S2);
  not not_3 (not_3_out, OPCODE2);
  not not_4 (not_4_out, S2);
  not not_5 (not_5_out, OPCODE3);
  not not_6 (not_6_out, S2);
  not not_7 (not_7_out, S3);
  not not_8 (not_8_out, S1);
  not not_9 (not_9_out, S3);
  not not_10 (not_10_out, S1);
  not not_11 (not_11_out, S2);
  not not_12 (not_12_out, S3);
  or or_1 (MEM_ACC, S3, S2);
  not not_13 (not_13_out, S1);
  not not_14 (not_14_out, S2);
  not not_15 (not_15_out, S3);
  not not_16 (not_16_out, S1);
  not not_17 (not_17_out, S2);
  not not_18 (not_18_out, S3);
  not not_19 (not_19_out, S3);
  or or_2 (S1_NEXT, and_1_out, and_2_out);
  and and_3 (and_3_out, not_1_out, not_2_out, S3);
  and and_4 (and_4_out, not_3_out, not_4_out, S3);
  and and_5 (and_5_out, not_5_out, not_6_out, S3);
  and and_6 (and_6_out, S2, not_7_out);
  and and_7 (and_7_out, not_8_out, not_9_out);
  and and_8 (and_8_out, OPCODE1, OPCODE2, OPCODE3, not_10_out);
  and and_9 (PC, S1, not_11_out, not_12_out);
  and and_10 (IR, not_13_out, not_14_out, not_15_out);
  and and_11 (and_11_out, not_16_out, not_17_out, S3);
  and and_12 (and_12_out, S2, not_18_out);
  and and_13 (WB, S1, not_19_out);
  or or_3 (S2_NEXT, and_3_out, and_4_out, and_5_out, and_6_out);
  or or_4 (S3_NEXT, and_7_out, and_8_out);
  or or_5 (DR, and_11_out, and_12_out);
endmodule

// BASIC
module ALU_BASIC_INST (
  input  LINK,
  input  [11:0] ACC,
  input  [11:0] DATA,
  input  [7:0] PC,
  input  [7:0] MEM_ADDR,
  input  [2:0] ALU_CONTROL,
  input  IB,
  input  [7:0] M_a,
  output LINK_OUT,
  output [11:0] ACC_OUT,
  output [11:0] DATA_OUT,
  output [7:0] NEXT_PC
);

  wire ADD_LINK, and_2_out, comparator_1_eq, comparator_2_eq, comparator_3_eq, not_1_out;
  wire [7:0] adder_3_out, adder_4_out, adder_5_out, ISZ_PC, JMP_PC, JMS_PC, multiplexer_3_out;
  wire [11:0] ADD_ACC, AND_ACC, ISZ_DATA, JMS_DATA;

  assign AND_ACC = ACC & DATA;  // AND_Gate and_1, 12 bits wide
  Adder #(.width(12)) adder_1 (.a(ACC), .b(DATA), .out(ADD_ACC));  // open: cin, cout
  Comparator #(.width(1)) comparator_1 (.a(ACC[11]), .b(DATA[11]), .eq(comparator_1_eq));  // open: gt, lt
  Comparator #(.width(1)) comparator_2 (.a(ACC[11]), .b(ADD_ACC[11]), .eq(comparator_2_eq));  // open: gt, lt
  Adder #(.width(12)) adder_2 (.a(DATA), .b(12'h1), .out(ISZ_DATA));  // open: cin, cout
  Comparator #(.width(12)) comparator_3 (.a(ISZ_DATA), .b({12{1'b0}}), .eq(comparator_3_eq));  // open: gt, lt
  Adder adder_3 (.a(PC), .b(8'h1), .out(adder_3_out));  // open: cin, cout
  Multiplexer #(.width(8), .enable("false")) multiplexer_1 (
    .in0(adder_3_out), .in1(adder_4_out), .out(ISZ_PC), .sel(comparator_3_eq));
  Adder adder_4 (.a(8'h2), .b(PC), .out(adder_4_out));  // open: cin, cout
  and and_2 (and_2_out, comparator_1_eq, ~comparator_2_eq);  // AND_Gate
  Multiplexer #(.enable("false")) multiplexer_2 (.in0(LINK), .in1(not_1_out), .out(ADD_LINK), .sel(and_2_out));
  not not_1 (not_1_out, LINK);
  Adder adder_5 (.a(PC), .b(8'h1), .out(adder_5_out));  // open: cin, cout
  Multiplexer #(.width(8), .enable("false")) multiplexer_3 (
    .in0(MEM_ADDR), .in1(M_a), .out(multiplexer_3_out), .sel(IB));
  assign JMS_DATA = {{4{1'b0}}, adder_5_out};  // Bit_Extender bit_extender_1
  Adder adder_6 (.a(multiplexer_3_out), .b(8'h1), .out(JMS_PC));  // open: cin, cout
  Multiplexer #(.select(3), .width(12), .enable("false")) multiplexer_4 (
    .in0(AND_ACC), .in1(ADD_ACC), .in3({12{1'b0}}), .out(ACC_OUT), .sel(ALU_CONTROL));  // open: in2, in4, in5, in6, in7
  Multiplexer #(.select(3), .width(12), .enable("false")) multiplexer_5 (
    .in2(ISZ_DATA), .in3(ACC), .in4(JMS_DATA), .in6(DATA), .out(DATA_OUT), .sel(ALU_CONTROL));  // open: in0, in1, in5, in7
  Multiplexer #(.width(8), .enable("false")) multiplexer_6 (.in0(MEM_ADDR), .in1(M_a), .out(JMP_PC), .sel(IB));
  Multiplexer #(.select(3), .enable("false")) multiplexer_7 (
    .in1(ADD_LINK), .out(LINK_OUT), .sel(ALU_CONTROL));  // open: in0, in2, in3, in4, in5, in6, in7
  Multiplexer #(.select(3), .width(8), .enable("false")) multiplexer_8 (
    .in2(ISZ_PC), .in4(JMS_PC), .in5(JMP_PC), .out(NEXT_PC), .sel(ALU_CONTROL));  // open: in0, in1, in3, in6, in7
  Multiplexer #(.width(8), .enable("false")) multiplexer_9 (.sel(IB));  // open: in0, in1, out

  // Other names for the same wires on the sheet: DCA_DATA[11:0] = ACC; OUT_DATA[11:0] = DATA; PC_OUT[7:0] = NEXT_PC
endmodule

// GRP1
module ALU_GRP1 (
  input  [7:0] MINTS,
  input  LINK,
  input  [11:0] ACC,
  output [11:0] ACC_OUT,
  output LINK_OUT
);

  wire BIT0, multiplexer_1_out, multiplexer_9_out, multiplexer_10_out, not_2_out;
  wire [11:0] adder_1_out, multiplexer_2_out, multiplexer_4_out, multiplexer_5_out, multiplexer_6_out,
       multiplexer_7_out, not_1_out;

  Multiplexer #(.enable("false")) multiplexer_1 (.in0(LINK), .in1(1'b0), .out(multiplexer_1_out), .sel(MINTS[6]));
  Multiplexer #(.width(12), .enable("false")) multiplexer_2 (
    .in0(ACC), .in1({12{1'b0}}), .out(multiplexer_2_out), .sel(MINTS[7]));
  assign not_1_out = ~multiplexer_2_out;  // NOT_Gate not_1, 12 bits wide
  Multiplexer #(.enable("false")) multiplexer_3 (.in0(multiplexer_1_out), .in1(not_2_out), .out(BIT0), .sel(MINTS[4]));
  not not_2 (not_2_out, multiplexer_1_out);
  Multiplexer #(.width(12), .enable("false")) multiplexer_4 (
    .in0(multiplexer_2_out), .in1(not_1_out), .out(multiplexer_4_out), .sel(MINTS[5]));
  Multiplexer #(.width(12), .enable("false")) multiplexer_5 (
    .in0(multiplexer_4_out), .in1(adder_1_out), .out(multiplexer_5_out), .sel(MINTS[0]));
  Adder #(.width(12)) adder_1 (.a(multiplexer_4_out), .b(12'h1), .out(adder_1_out));  // open: cin, cout
  Multiplexer #(.width(12), .enable("false")) multiplexer_6 (
    .in0({multiplexer_5_out[10:0], BIT0}), .in1({multiplexer_5_out[9:0], BIT0, multiplexer_5_out[11]}),
    .out(multiplexer_6_out), .sel(MINTS[1]));
  Multiplexer #(.width(12), .enable("false")) multiplexer_7 (
    .in0({BIT0, multiplexer_5_out[11:1]}), .in1({multiplexer_5_out[0], BIT0, multiplexer_5_out[11:2]}),
    .out(multiplexer_7_out), .sel(MINTS[1]));
  Multiplexer #(.select(2), .width(12), .enable("false")) multiplexer_8 (
    .in0(multiplexer_5_out), .in1(multiplexer_6_out), .in2(multiplexer_7_out), .in3(multiplexer_5_out),
    .out(ACC_OUT), .sel(MINTS[3:2]));
  Multiplexer #(.enable("false")) multiplexer_9 (
    .in0(multiplexer_5_out[11]), .in1(multiplexer_5_out[10]), .out(multiplexer_9_out), .sel(MINTS[1]));
  Multiplexer #(.enable("false")) multiplexer_10 (
    .in0(multiplexer_5_out[0]), .in1(multiplexer_5_out[1]), .out(multiplexer_10_out), .sel(MINTS[1]));
  Multiplexer #(.select(2), .enable("false")) multiplexer_11 (
    .in0(BIT0), .in1(multiplexer_9_out), .in2(multiplexer_10_out), .in3(BIT0), .out(LINK_OUT),
    .sel(MINTS[3:2]));

  // Other names for the same wires on the sheet: BIT4 = MINTS[4]
endmodule

// GRP2
module ALU_GRP2 (
  input  [7:0] Instruction,
  input  [11:0] ACC,
  input  LNK,
  input  [7:0] PC,
  output [11:0] ACCout,
  output [7:0] PCout
);

  wire and_1_out, comparator_1_eq, comparator_1_lt, comparator_2_eq, multiplexer_4_out, multiplexer_5_out,
       multiplexer_6_out, multiplexer_7_out, not_1_out, or_1_out;
  wire [7:0] adder_1_out, adder_2_out, multiplexer_1_out;

  Adder adder_1 (.a(PC), .b(8'h1), .out(adder_1_out));  // open: cin, cout
  Adder adder_2 (.a(PC), .b(8'h2), .out(adder_2_out));  // open: cin, cout
  Multiplexer #(.width(8), .enable("false")) multiplexer_1 (
    .in0(adder_1_out), .in1(adder_2_out), .out(multiplexer_1_out), .sel(multiplexer_7_out));
  Multiplexer #(.width(8), .enable("false")) multiplexer_2 (
    .in0(multiplexer_1_out), .in1(PC), .out(PCout), .sel(Instruction[1]));
  Multiplexer #(.width(12), .enable("false")) multiplexer_3 (
    .in0(ACC), .in1({12{1'b0}}), .out(ACCout), .sel(Instruction[7]));
  Comparator #(.width(12)) comparator_1 (
    .a(ACC), .b({12{1'b0}}), .eq(comparator_1_eq), .lt(comparator_1_lt));  // open: gt
  Comparator #(.width(1)) comparator_2 (.a(LNK), .b(1'b0), .eq(comparator_2_eq));  // open: gt, lt
  not not_1 (not_1_out, comparator_2_eq);
  Multiplexer #(.enable("false")) multiplexer_4 (
    .in0(1'b0), .in1(comparator_1_lt), .out(multiplexer_4_out), .sel(Instruction[6]));
  Multiplexer #(.enable("false")) multiplexer_5 (
    .in0(1'b0), .in1(comparator_1_eq), .out(multiplexer_5_out), .sel(Instruction[5]));
  Multiplexer #(.enable("false")) multiplexer_6 (
    .in0(1'b0), .in1(not_1_out), .out(multiplexer_6_out), .sel(Instruction[4]));
  or or_1 (or_1_out, multiplexer_4_out, multiplexer_5_out, multiplexer_6_out);
  and and_1 (and_1_out, ~multiplexer_4_out, ~multiplexer_5_out, ~multiplexer_6_out);  // AND_Gate
  Multiplexer #(.enable("false")) multiplexer_7 (
    .in0(or_1_out), .in1(and_1_out), .out(multiplexer_7_out), .sel(Instruction[3]));
endmodule

module EX_OUT_LOGIC (
  input  GRP,
  input  OPCODE1,
  input  OPCODE2,
  input  OPCODE3,
  output LNK_SEL,
  output ACC_SEL,
  output ACC_SEL2,
  output PC_SEL,
  output PC_SEL2
);

  wire and_3_out, and_4_out, not_1_out, not_2_out, not_3_out, not_4_out, not_5_out;

  not not_1 (not_1_out, GRP);
  and and_1 (ACC_SEL, GRP, OPCODE1, OPCODE2, OPCODE3);
  not not_2 (not_2_out, GRP);
  and and_2 (PC_SEL, GRP, OPCODE1, OPCODE2, OPCODE3);
  not not_3 (not_3_out, OPCODE1);
  and and_3 (and_3_out, not_3_out, OPCODE2, not_4_out);
  not not_4 (not_4_out, OPCODE3);
  and and_4 (and_4_out, OPCODE1, not_5_out);
  not not_5 (not_5_out, OPCODE2);
  and and_5 (LNK_SEL, not_1_out, OPCODE1, OPCODE2, OPCODE3);
  and and_6 (ACC_SEL2, not_2_out, OPCODE1, OPCODE2, OPCODE3);
  or or_1 (PC_SEL2, and_3_out, and_4_out);
endmodule

module MEM_SEL_LOGIC (
  input  IB,
  input  STATE2,
  input  STATE4,
  output MEM_SEL,
  output MEM_SEL2
);

  wire not_1_out, not_2_out;

  not not_1 (not_1_out, STATE2);
  not not_2 (not_2_out, STATE4);
  and and_1 (MEM_SEL, IB, not_1_out, STATE4);
  and and_2 (MEM_SEL2, IB, STATE2, not_2_out);
endmodule

module WB (
  input  WB,
  input  GRP_IB,
  input  OPCODE1,
  input  OPCODE2,
  input  OPCODE3,
  output LINK_WB,
  output ACC_WB,
  output MEM_WB
);

  wire and_1_out, and_2_out, and_3_out, and_4_out, and_5_out, and_6_out, not_1_out, not_2_out, not_3_out,
       not_4_out, not_5_out, not_6_out, not_7_out, not_8_out;

  not not_1 (not_1_out, OPCODE1);
  not not_2 (not_2_out, OPCODE2);
  not not_3 (not_3_out, GRP_IB);
  not not_4 (not_4_out, OPCODE1);
  not not_5 (not_5_out, OPCODE2);
  not not_6 (not_6_out, OPCODE1);
  not not_7 (not_7_out, OPCODE2);
  not not_8 (not_8_out, OPCODE3);
  and and_1 (and_1_out, WB, not_1_out, not_2_out, OPCODE3);
  and and_2 (and_2_out, WB, not_3_out, OPCODE1, OPCODE2, OPCODE3);
  and and_3 (and_3_out, WB, not_4_out, not_5_out);
  and and_4 (and_4_out, WB, OPCODE2, OPCODE3);
  and and_5 (and_5_out, WB, not_6_out, OPCODE2);
  and and_6 (and_6_out, WB, OPCODE1, not_7_out, not_8_out);
  or or_1 (LINK_WB, and_1_out, and_2_out);
  or or_2 (ACC_WB, and_3_out, and_4_out);
  or or_3 (MEM_WB, and_5_out, and_6_out);
endmodule
